# Fritzing sketch Untitled Sketch (saved by Fritzing 0.9.3b)

parts:
  M1 = DC Motor
  M2 = DC Motor
  Componente1 = Adafruit Motor/Stepper/Servo Shield [part_number="Adafruit #1438"]
  J1 = Basic Servo
  hc-sr1 = hc-sr04
  Componente3 = Bluetooth HC-06
  VCC1 = 4 x AAA Battery Mount

nets:
  N1: M1.pin_1, Componente1.M1B
  N2: M1.pin_2, Componente1.M1A
  N3: M2.pin_1, Componente1.M2A
  N4: M2.pin_2, Componente1.M2B
  N5: Componente1.VMOTOR, VCC1.+
  GND: Componente1.GND, J1.gnd, hc-sr1.GND, Componente3.GND
  VCC: Componente1.+5V, J1.vcc, hc-sr1.VCC
  N6: Componente1.D10, J1.pulse
  N7: Componente1.D0, Componente3.TXD
  N8: Componente1.D1, Componente3.RXD
  N9: Componente1.D6, hc-sr1.Echo
  N10: Componente1.D7, hc-sr1.Trig

custom parts:
  Adafruit Motor/Stepper/Servo Shield: The original Adafruit Motorshield kit is one of our most beloved kits, which is why we decided to make something even better. We have upgraded the shield kit to make the bestest, easiest way to drive DC and Stepper motors. This shield will make quick work of your next robotics project! We kept the ability to drive up to 4 DC motors or 2 stepper motors, but added many improvements: Instead of a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
